# Fritzing sketch SmartFarm (saved by Fritzing 0.9.4)
breadboards: 1

parts:
  S1 = Toggle Switch [package=THT]
  S2 = Pushbutton [package="[THT]"]
  M1 = DC Motor
  Part2 = Arduino Uno (Rev3) - ICSP
  Part3 = Bluetooth HC-05 Macho
  LCM1602_IIC1 = LCM1602 IIC [part_number="LCM1602 IIC" chip_label="LCM1602 IIC" package="DIP (Dual Inline) [THT]"]
  KY-2 = Keyes Relay [package=THT]
  Part4 = FC-28 Soil Hygrometer Module - Probe
  Part5 = FC-28 Soil Hygrometer Module
  LCD1 = LCD screen

nets:
  N1: S1.L1, S2.Pin_1, S2.Pin_2, KY-2.NC
  VCC: S1.COM, S2.Pin_3, S2.Pin_4, Part2.5V, Part3.VCC, LCM1602_IIC1.VCC, KY-2.power, KY-2.NO, Part5.VCC
  GND: M1.pin_1, Part2.GND, Part3.GND, LCM1602_IIC1.GND, KY-2.ground, Part5.GND
  N2: M1.pin_2, KY-2.C
  N3: Part2.A0, Part5.AO
  N4: Part2.A4/SDA, LCM1602_IIC1.SDA
  N5: Part2.A5/SCL, LCM1602_IIC1.SCL
  N6: Part2.D0/RX, Part3.TXD
  N7: Part2.D1/TX, Part3.RXD
  N8: Part2.D7, KY-2.signal
  VSS: LCM1602_IIC1.VSS, LCD1.VSS
  VDD: LCM1602_IIC1.VDD, LCD1.VDD
  N9: LCM1602_IIC1.V0, LCD1.V0
  N10: LCM1602_IIC1.RS, LCD1.RS
  N11: LCM1602_IIC1.RW, LCD1.R/W
  N12: LCM1602_IIC1.E, LCD1.E
  N13: LCM1602_IIC1.D0, LCD1.DB0
  N14: LCM1602_IIC1.D1, LCD1.DB1
  N15: LCM1602_IIC1.D2, LCD1.DB2
  N16: LCM1602_IIC1.D3, LCD1.DB3
  N17: LCM1602_IIC1.D4, LCD1.DB4
  N18: LCM1602_IIC1.D5, LCD1.DB5
  N19: LCM1602_IIC1.D6, LCD1.DB6
  N20: LCM1602_IIC1.D7, LCD1.DB7
  N21: LCM1602_IIC1.A, LCD1.LED+
  N22: LCM1602_IIC1.K, LCD1.LED-
  N23: LCM1602_IIC1.LED_A, LCM1602_IIC1.LED_B
  N24: Part4.POS, Part5.POS
  N25: Part4.NEG, Part5.NEG

custom parts:
  LCM1602 IIC: I2C-Module to use a 1602 or 2004 LCD on with the wire.h libory Serial LCD Modul
  Keyes Relay: The Keyes 5V relay module is suitable for SCM development, home appliance control. It uses a 5V~12V TIL control signal which can control DC / AC signal.
  FC-28 Soil Hygrometer Module - Probe: The FC-28 is a soil hygrometer module that uses the Texas Instruments LM393 comparator chip to provide an analog measurement of soil humidity.
  FC-28 Soil Hygrometer Module: The FC-28 is a soil hygrometer module that uses the Texas Instruments LM393 comparator chip to provide an analog measurement of soil humidity. The digital output is high when soil moisture is over a certain threshold, as determined by adjusting the potentiometer.
